# Fritzing sketch SomfyProxy schematics (saved by Fritzing 0.9.2b)
breadboards: 1

parts:
  Raspberry_Pi_pinout = RaspIO Duino
  R3 = Resistor [tolerance=±5% resistance=330 package="2010 [SMD]"]
  R1 = Resistor [tolerance=±5% resistance=330 package="2010 [SMD]"]
  R4 = Resistor [tolerance=±5% resistance=330 package="2010 [SMD]"]
  R2 = Resistor [tolerance=±5% resistance=330 package="2010 [SMD]"]
  U1 = TLP621 [package=THT]
  U3 = TLP621 [package=THT]
  U4 = TLP621 [package=THT]
  U2 = TLP621 [package=THT]
  up = Pushbutton [package="[THT]"]
  stop = Pushbutton [package="[THT]"]
  down = Pushbutton [package="[THT]"]
  channel = Pushbutton [package="[THT]"]

nets:
  GND: Raspberry_Pi_pinout.GND, Raspberry_Pi_pinout.pin3, U1.Pin_2, U1.Pin_3, U3.Pin_2, U3.Pin_3, U4.Pin_2, U4.Pin_3, U2.Pin_2, U2.Pin_3
  3.3V: Raspberry_Pi_pinout.3V3
  N1: Raspberry_Pi_pinout.GPIO14, Raspberry_Pi_pinout.tx(pi), R4.Pin_0
  N2: Raspberry_Pi_pinout.GPIO_18, R3.Pin_0
  N3: Raspberry_Pi_pinout.GPIO_23, R2.Pin_0
  N4: Raspberry_Pi_pinout.GPIO_24, R1.Pin_0
  N5: R3.Pin_1, U3.Pin_1
  N6: R1.Pin_1, U1.Pin_1
  N7: R4.Pin_1, U4.Pin_1
  N8: R2.Pin_1, U2.Pin_1
  N9: U1.Pin_4, up.Pin_3, up.Pin_4
  N10: U3.Pin_4, down.Pin_3, down.Pin_4
  N11: U4.Pin_4, channel.Pin_3, channel.Pin_4
  N12: U2.Pin_4, stop.Pin_3

notes:
  Somfy remote
  The Somfy remote sketch only shows which wires connect to the remote.
